# Fritzing sketch Water cooling controller (saved by Fritzing 0.9.9b)
circuit board: 9.34041cm x 6.08891cm
stripboards: 1

parts:
  FAN2 = Header 4 [package=molex-1x4_lock]
  FAN3 = Header 4 [package=molex-1x4_lock]
  TH1_(Inlet) = double row male pin header, 2 pins [form="♂ (male)"]
  J1 = female pin header, 15 pins [form="♀ (female)"]
  R5 = Resistor [tolerance=±10% resistance=10k package=THT]
  2_8_TFT_SPI_240X320_V1_2 = male pin header, 9 pins [form="♂ (male)"]
  SATA_Power = male pin header, 5 pins [form="♂ (male)"]
  R4 = Resistor [tolerance=±10% resistance=10k package=THT]
  R6 = Resistor [tolerance=±10% resistance=3.3k package=THT]
  FAN1 = Header 4 [package=molex-1x4_lock]
  J2 = female pin header, 15 pins [form="♀ (female)"]
  M1 = DOIT Esp32 DevKit v1 (30 pins long, 11 pins width) [part_number=ESP32S-PIN30]
  TH2_(Outlet) = double row male pin header, 2 pins [form="♂ (male)"]
  PUMP = Header 4 [package=molex-1x4_lock]

nets:
  N1: FAN2.1, FAN3.1, TH1_(Inlet).pin1, J1.pin14, 2_8_TFT_SPI_240X320_V1_2.pin1, SATA_Power.pin2, SATA_Power.pin4, FAN1.1, J2.pin2, M1.GND, TH2_(Outlet).pin1, PUMP.1
  N2: FAN2.2, FAN3.2, SATA_Power.pin5, FAN1.2, PUMP.2
  N3: FAN2.3, J1.pin9, M1.D26
  N4: FAN2.4, FAN3.4, FAN1.4, J2.pin6, M1.RX2, PUMP.4
  N5: FAN3.3, J1.pin10, M1.D27
  N6: TH1_(Inlet).pin2, J1.pin4, R4.Pin_1, M1.D34
  N7: J1.pin1, M1.EN
  N8: J1.pin2, M1.VP
  N9: J1.pin3, M1.VN
  N10: J1.pin5, R5.Pin_1, M1.D35, TH2_(Outlet).pin2
  N11: J1.pin6, M1.D32
  N12: J1.pin7, M1.D33
  N13: J1.pin8, FAN1.3, M1.D25
  N14: J1.pin11, R6.Pin_1, M1.D14, PUMP.3
  N15: J1.pin12, M1.D12
  N16: J1.pin13, M1.D13
  N17: J1.pin15, 2_8_TFT_SPI_240X320_V1_2.pin6, SATA_Power.pin3, M1.VIN
  N18: R5.Pin_0, SATA_Power.pin1, R4.Pin_0, R6.Pin_0, J2.pin1, M1.3V3
  N19: 2_8_TFT_SPI_240X320_V1_2.pin2, J2.pin15, M1.D23
  N20: 2_8_TFT_SPI_240X320_V1_2.pin3, J2.pin14, M1.D22
  N21: 2_8_TFT_SPI_240X320_V1_2.pin4, J2.pin5, M1.D4
  N22: 2_8_TFT_SPI_240X320_V1_2.pin5, J2.pin3, M1.D15
  N23: 2_8_TFT_SPI_240X320_V1_2.pin7, J2.pin10, M1.D19
  N24: 2_8_TFT_SPI_240X320_V1_2.pin8, J2.pin9, M1.D18
  N25: 2_8_TFT_SPI_240X320_V1_2.pin9, J2.pin8, M1.D5
  N26: J2.pin4, M1.D2
  N27: J2.pin7, M1.TX2
  N28: J2.pin11, M1.D21
  N29: J2.pin12, M1.RX0
  N30: J2.pin13, M1.TX0

notes:
  GND
  VCC
  RESET
  MOSI
  MISO
  DC
  LED
  SCK
  CS
  SENSE
  PWM
  3V
  5V
  12V

custom parts:
  DOIT Esp32 DevKit v1 (30 pins long, 11 pins width): The DOIT Esp32 DevKit v1 is one of the development board created by DOIT to evaluate the ESP-WROOM-32 module. It is based on the ESP32 microcontroller that boasts Wifi, Bluetooth, Ethernet and Low Power support all in a single chip. (vanepp) made breadboard work, adjusted pin numbering and labels and reduced size of schematic and cleaned up pcb. This chip is 30pins long (2 x15) and 11 pins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
